# Fritzing sketch LCD1602 (saved by Fritzing 0.9.6b)
breadboards: 1

parts:
  U1 = keyestudio ESP32 plus development board [part_number=ESP32]
  LCD1 = LCD screen
  R1 = Trimmer Potentiometer [maximum_resistance=10kΩ package=THT]

nets:
  N1: U1.io26, LCD1.DB7
  N2: U1.io25, LCD1.DB6
  N3: U1.io17, LCD1.DB5
  N4: U1.io16, LCD1.DB4
  N5: U1.io23, LCD1.E
  N6: U1.io19, LCD1.RS
  GND: U1.GND, LCD1.VSS, LCD1.R/W, R1.leg1
  5V: U1.5V, U1.VCC, LCD1.VDD, R1.leg2
  N7: LCD1.V0, R1.wiper

custom parts:
  keyestudio ESP32 plus development board: keyestudio ESP32 plus STEM makers development board 2.4GHz dual-mode WiFi + bluetooth dual cores microcontroller
